// Logisim project IC_74181_ALU.circ as structural Verilog: 1 circuit, main circuit main
module main (
  input  [3:0] A3_A2_A1_A0,
  input  M,
  input  [3:0] B3_B2_B1_B0,
  input  Cn,
  input  [3:0] S3_S2_S1_S0,
  output P,
  output Cn___4,
  output A___B,
  output [3:0] F3_F2_F1_F0
);

  wire and_1_out, and_2_out, and_3_out, and_4_out, and_5_out, and_6_out, and_7_out, and_8_out, and_9_out,
       and_11_out, and_12_out, and_13_out, and_14_out, and_15_out, and_16_out, and_17_out, and_18_out,
       and_19_out, and_20_out, and_21_out, and_22_out, and_23_out, and_24_out, and_25_out, and_26_out,
       and_27_out, and_28_out, and_29_out, and_30_out, and_31_out, and_32_out, and_33_out, and_34_out,
       and_35_out, and_36_out, and_37_out, and_38_out, nand_1_out, nand_3_out, nor_1_out, nor_2_out,
       nor_3_out, nor_4_out, nor_5_out, nor_6_out, nor_7_out, nor_8_out, nor_9_out, nor_10_out, nor_11_out,
       nor_12_out, not_2_out, not_3_out, not_4_out, not_5_out, not_6_out, not_7_out, not_8_out, not_9_out,
       not_10_out;
  wire [3:0] not_1_out, not_11_out;

  assign not_1_out = ~A3_A2_A1_A0;  // NOT_Gate not_1, 4 bits wide
  not not_2 (not_2_out, Cn);
  nand nand_1 (nand_1_out, not_2_out, M);
  xor xor_1 (F3_F2_F1_F0[0], nand_1_out, and_3_out);
  and and_1 (and_1_out, not_1_out[0], not_1_out[0]);
  not not_3 (not_3_out, nor_1_out);
  and and_2 (and_2_out, not_11_out[0], S3_S2_S1_S0[0]);
  nor nor_1 (nor_1_out, and_1_out, and_2_out, and_4_out);
  and and_3 (and_3_out, not_3_out, nor_3_out);
  not not_4 (not_4_out, not_11_out[0]);
  and and_4 (and_4_out, S3_S2_S1_S0[1], not_4_out);
  and and_5 (and_5_out, M, nor_1_out);
  nor nor_2 (nor_2_out, and_5_out, and_7_out);
  xor xor_2 (F3_F2_F1_F0[1], nor_2_out, and_9_out);
  and and_6 (and_6_out, not_4_out, S3_S2_S1_S0[2], not_1_out[0]);
  nor nor_3 (nor_3_out, and_6_out, and_8_out);
  and and_7 (and_7_out, M, nor_3_out, not_2_out);
  and and_8 (and_8_out, not_1_out[0], not_11_out[0], S3_S2_S1_S0[3]);
  not not_5 (not_5_out, nor_4_out);
  and and_9 (and_9_out, not_5_out, nor_6_out);
  and and_10 (A___B, F3_F2_F1_F0[0], F3_F2_F1_F0[1], F3_F2_F1_F0[2], F3_F2_F1_F0[3]);
  and and_11 (and_11_out, not_1_out[1], not_1_out[1]);
  and and_12 (and_12_out, M, nor_4_out);
  and and_13 (and_13_out, not_11_out[1], S3_S2_S1_S0[0]);
  nor nor_4 (nor_4_out, and_11_out, and_13_out, and_15_out);
  and and_14 (and_14_out, M, nor_1_out, nor_6_out);
  nor nor_5 (nor_5_out, and_12_out, and_14_out, and_16_out);
  xor xor_3 (F3_F2_F1_F0[2], nor_5_out, and_19_out);
  not not_6 (not_6_out, not_11_out[1]);
  and and_15 (and_15_out, S3_S2_S1_S0[1], not_6_out);
  not not_7 (not_7_out, nor_7_out);
  and and_16 (and_16_out, M, not_2_out, nor_3_out, nor_6_out);
  and and_17 (and_17_out, not_6_out, S3_S2_S1_S0[2], not_1_out[1]);
  nor nor_6 (nor_6_out, and_17_out, and_20_out);
  and and_18 (and_18_out, M, nor_7_out);
  and and_19 (and_19_out, not_7_out, nor_9_out);
  and and_20 (and_20_out, not_1_out[1], not_11_out[1], S3_S2_S1_S0[3]);
  and and_21 (and_21_out, M, nor_4_out, nor_9_out);
  and and_22 (and_22_out, not_11_out[2], S3_S2_S1_S0[0]);
  and and_23 (and_23_out, not_1_out[2], not_1_out[2]);
  nor nor_7 (nor_7_out, and_23_out, and_22_out, and_25_out);
  and and_24 (and_24_out, M, nor_3_out, nor_6_out, nor_9_out);
  nor nor_8 (nor_8_out, and_18_out, and_21_out, and_24_out, and_26_out);
  xor xor_4 (F3_F2_F1_F0[3], nor_8_out, and_28_out);
  and and_25 (and_25_out, S3_S2_S1_S0[1], not_8_out);
  and and_26 (and_26_out, M, not_2_out, nor_3_out, nor_6_out, nor_9_out);
  not not_8 (not_8_out, not_11_out[2]);
  and and_27 (and_27_out, not_8_out, S3_S2_S1_S0[2], not_1_out[2]);
  not not_9 (not_9_out, nor_10_out);
  and and_28 (and_28_out, not_9_out, nor_11_out);
  and and_29 (and_29_out, not_1_out[2], not_11_out[2], S3_S2_S1_S0[3]);
  nor nor_9 (nor_9_out, and_27_out, and_29_out);
  and and_30 (and_30_out, not_1_out[3], not_1_out[3]);
  nand nand_2 (P, nor_3_out, nor_6_out, nor_9_out, nor_11_out);
  and and_31 (and_31_out, not_11_out[3], S3_S2_S1_S0[0]);
  nor nor_10 (nor_10_out, and_30_out, and_31_out, and_32_out);
  nand nand_3 (nand_3_out, not_2_out, nor_3_out, nor_6_out, nor_9_out, nor_11_out);
  nand nand_4 (Cn___4, nand_3_out, nor_12_out);
  and and_32 (and_32_out, S3_S2_S1_S0[1], not_10_out);
  and and_33 (and_33_out, nor_1_out, nor_6_out, nor_9_out, nor_11_out);
  not not_10 (not_10_out, not_11_out[3]);
  and and_34 (and_34_out, not_10_out, S3_S2_S1_S0[2], not_1_out[3]);
  and and_35 (and_35_out, nor_4_out, nor_9_out, nor_11_out);
  and and_36 (and_36_out, not_1_out[3], not_11_out[3], S3_S2_S1_S0[3]);
  nor nor_11 (nor_11_out, and_34_out, and_36_out);
  and and_37 (and_37_out, nor_7_out, nor_11_out);
  nor nor_12 (nor_12_out, and_33_out, and_35_out, and_37_out, and_38_out);
  and and_38 (and_38_out, nor_10_out, nor_10_out);
  assign not_11_out = ~B3_B2_B1_B0;  // NOT_Gate not_11, 4 bits wide

  // Notes on the sheet:
  //   IC 74181
endmodule
